# Fritzing sketch current_sensor (saved by Fritzing 0.9.3b)
breadboards: 1

parts:
  R1 = Resistor [tolerance=±5% resistance=300 package=THT]
  Q1 = PNP-Transistor [package="TO92 [THT]"]
  PullUp = WeMos D1 Mini
  L1 = Inductor [package="0603 [SMD]"]
  C1 = Electrolytic Capacitor [capacitance=4.7µF voltage=50V package="0405 [SMD, electrolytic]"]
  R2 = Resistor [tolerance=±5% resistance=10k package=THT]
  D1 = Rectifier Diode [part_number=1N4001 package="300 mil [THT]"]

nets:
  N1: R1.Pin_0, L1.pin_0, C1.+, R2.Pin_1
  N2: R1.Pin_1, Q1.B
  N3: Q1.E, PullUp.D0
  N4: Q1.C, C1.-, R2.Pin_0, D1.anode
  N5: L1.pin_1, D1.cathode
