# Fritzing sketch pzem_mqtt (saved by Fritzing 0.9.3b)
breadboards: 1

parts:
  WeMos_D1_Mini1 = WeMos D1 Mini
  Part1 = blueIOT core
  M1 = Pzem-004t
  Mod1 = generic-ac-power-supply [package=THT]
  L1 = Toroide Bifilar [package="Bifilar Wound"]

nets:
  N1: WeMos_D1_Mini1.3V3, Part1.D8, Part1.D10
  5V: WeMos_D1_Mini1.5V, Part1.D5, Part1.TXD, M1.5V, Mod1.pin3#2
  N2: WeMos_D1_Mini1.A0, Part1.P21
  N3: WeMos_D1_Mini1.D0, Part1.RESET
  N4: WeMos_D1_Mini1.D1, Part1.A4
  N5: WeMos_D1_Mini1.D2, Part1.A5
  N6: WeMos_D1_Mini1.D3, Part1.RXD
  N7: WeMos_D1_Mini1.D4, Part1.GND
  N8: WeMos_D1_Mini1.D5, Part1.VCC, M1.RX
  N9: WeMos_D1_Mini1.D6, Part1.MISO, M1.TX
  N10: WeMos_D1_Mini1.D7, Part1.SCK
  N11: WeMos_D1_Mini1.D8, Part1.MOSI
  N12: WeMos_D1_Mini1.G, Part1.D2, M1.GND, Mod1.pin3#3
  N13: WeMos_D1_Mini1.RST, Part1.P22
  N14: WeMos_D1_Mini1.RX, Part1.A0
  N15: WeMos_D1_Mini1.TX, Part1.DTR
  N16: M1.NIN, L1.pin1
  N17: M1.NOUT, L1.pin3

notes:
  Coil
  ~ 220-240V

custom parts:
  Pzem-004t: Pzem-004t used for measuring AC voltage, current, active power, frequency, power factor and active energy, the module is without display function, the data is read through the TTL interface.
  generic-ac-power-supply: Generic ac power supply module. Use as is, or customize the svgs to fit your particular device (as they are all different.) Provides AC input and single DC output. PCB is generic and will need modifications if you intend to do a pcb mount.
  Toroide Bifilar: Toroide Bifilar para RF
